# Fritzing sketch Breadboard (saved by Fritzing 0.9.3b)
circuit board: 8.46667cm x 5.64444cm
breadboards: 1

parts:
  U2 = ESP8266 WiFi Module [part_number=ESP8266]
  U3 = LIPO-2000mAh [package=lipo-2000]
  U4 = V_REG_LD1117VXX [package=78xxl]
  S1 = Pushbutton [package="[THT]"]
  Part1 = FTDI Basic Programmer

nets:
  N1: U2.RXD, Part1.TXO
  N2: U2.VCC, U2.CH_PD, U4.OUT
  N3: U2.GPIO_0, S1.Pin_1, S1.Pin_2
  GND: U2.GND, U3.-, U4.GND, S1.Pin_3, S1.Pin_4
  N4: U2.TXD, Part1.RXI
  N5: U3.+, U4.IN

custom parts:
  ESP8266 WiFi Module: Generic WiFi Module based on the ESP8266 with onboard PCB antenna and UART communications
